// Logisim project t3lc.circ as structural Verilog: 6 circuits, main circuit test_t3lc_mem_reg
module alu (
  input  ENA,
  input  [4:0] OP,
  input  CLK,
  input  RESET,
  input  [7:0] A,
  input  [7:0] B,
  output [7:0] DATA
);

  wire adder_1_cout, comparator_1_eq, comparator_1_gt, decoder_1_out0, decoder_1_out1, decoder_1_out2,
       decoder_1_out3, decoder_1_out4, decoder_1_out5, decoder_1_out6, decoder_1_out7, decoder_1_out8,
       decoder_1_out9, decoder_1_out10, decoder_1_out11, decoder_1_out12, decoder_1_out13, decoder_1_out14,
       decoder_1_out15, or_3_out, subtractor_1_bout;
  wire [7:0] ACC_q, adder_1_out, and_1_out, bit_extender_1_out, bit_extender_2_out, bit_extender_3_out,
       bit_extender_4_out, controlled_buffer_1_out, divider_1_out, divider_1_rem, multiplexer_1_out,
       multiplier_1_cout, multiplier_1_out, negator_1_out, not_1_out, or_1_out, or_2_out, shifter_1_out,
       shifter_2_out, shifter_3_out, shifter_4_out, subtractor_1_out, xor_1_out;

  Adder adder_1 (.a(A), .b(B), .out(adder_1_out), .cin(ACC_q[0]), .cout(adder_1_cout));
  Subtractor subtractor_1 (.a(A), .b(B), .out(subtractor_1_out), .bin(ACC_q[0]), .bout(subtractor_1_bout));
  Multiplier multiplier_1 (.a(A), .b(B), .out(multiplier_1_out), .cin(ACC_q), .cout(multiplier_1_cout));
  Divider divider_1 (.a(A), .b(B), .out(divider_1_out), .upper(ACC_q), .rem(divider_1_rem));
  assign and_1_out = A & B;  // AND_Gate and_1, 8 bits wide
  assign or_1_out = A | B;  // OR_Gate or_1, 8 bits wide
  assign xor_1_out = A ^ B;  // XOR_Gate xor_1, 8 bits wide
  assign not_1_out = ~A;  // NOT_Gate not_1, 8 bits wide
  Shifter shifter_1 (.in(A), .\dist (3'b001), .out(shifter_1_out));
  Shifter shifter_2 (.in(A), .\dist (B[2:0]), .out(shifter_2_out));
  Shifter shifter_3 (.in(A), .\dist (3'b001), .out(shifter_3_out));
  Shifter #(.shift("lr")) shifter_4 (.in(A), .\dist (B[2:0]), .out(shifter_4_out));
  Negator negator_1 (.in(A), .out(negator_1_out));
  Comparator comparator_1 (.a(A), .b(B), .gt(comparator_1_gt), .eq(comparator_1_eq));  // open: lt
  assign bit_extender_1_out = {{7{1'b0}}, adder_1_cout};  // Bit_Extender bit_extender_1
  assign bit_extender_2_out = {{7{1'b0}}, subtractor_1_bout};  // Bit_Extender bit_extender_2
  assign or_2_out = 8'h1 | shifter_3_out;  // OR_Gate or_2, 8 bits wide
  assign bit_extender_3_out = {{7{1'b0}}, comparator_1_gt};  // Bit_Extender bit_extender_3
  assign bit_extender_4_out = {{7{1'b0}}, comparator_1_eq};  // Bit_Extender bit_extender_4
  assign controlled_buffer_1_out = decoder_1_out0 ? bit_extender_1_out : 8'bz;  // Controlled_Buffer controlled_buffer_1
  assign controlled_buffer_1_out = decoder_1_out1 ? bit_extender_2_out : 8'bz;  // Controlled_Buffer controlled_buffer_2
  assign controlled_buffer_1_out = decoder_1_out2 ? multiplier_1_cout : 8'bz;  // Controlled_Buffer controlled_buffer_3
  assign controlled_buffer_1_out = decoder_1_out3 ? divider_1_rem : 8'bz;  // Controlled_Buffer controlled_buffer_4
  Multiplexer #(.width(8)) multiplexer_1 (
    .in0(DATA), .in1(controlled_buffer_1_out), .out(multiplexer_1_out), .sel(or_3_out));
  or or_3 (or_3_out, decoder_1_out0, decoder_1_out1, decoder_1_out2, decoder_1_out3);
  Register ACC (.D(multiplexer_1_out), .en(OP[4]), .clk(CLK), .Q(ACC_q), .clr(RESET));
  Decoder #(.select(4)) decoder_1 (
    .out0(decoder_1_out0), .out1(decoder_1_out1), .out2(decoder_1_out2), .out3(decoder_1_out3),
    .out4(decoder_1_out4), .out5(decoder_1_out5), .out6(decoder_1_out6), .out7(decoder_1_out7),
    .out8(decoder_1_out8), .out9(decoder_1_out9), .out10(decoder_1_out10), .out11(decoder_1_out11),
    .out12(decoder_1_out12), .out13(decoder_1_out13), .out14(decoder_1_out14), .out15(decoder_1_out15),
    .sel(OP[3:0]), .en(ENA));
  assign DATA = decoder_1_out0 ? adder_1_out : 8'bz;  // Controlled_Buffer controlled_buffer_5
  assign DATA = decoder_1_out1 ? subtractor_1_out : 8'bz;  // Controlled_Buffer controlled_buffer_6
  assign DATA = decoder_1_out2 ? multiplier_1_out : 8'bz;  // Controlled_Buffer controlled_buffer_7
  assign DATA = decoder_1_out3 ? divider_1_out : 8'bz;  // Controlled_Buffer controlled_buffer_8
  assign DATA = decoder_1_out4 ? and_1_out : 8'bz;  // Controlled_Buffer controlled_buffer_9
  assign DATA = decoder_1_out5 ? or_1_out : 8'bz;  // Controlled_Buffer controlled_buffer_10
  assign DATA = decoder_1_out6 ? xor_1_out : 8'bz;  // Controlled_Buffer controlled_buffer_11
  assign DATA = decoder_1_out7 ? not_1_out : 8'bz;  // Controlled_Buffer controlled_buffer_12
  assign DATA = decoder_1_out8 ? shifter_1_out : 8'bz;  // Controlled_Buffer controlled_buffer_13
  assign DATA = decoder_1_out9 ? shifter_2_out : 8'bz;  // Controlled_Buffer controlled_buffer_14
  assign DATA = decoder_1_out10 ? or_2_out : 8'bz;  // Controlled_Buffer controlled_buffer_15
  assign DATA = decoder_1_out11 ? shifter_4_out : 8'bz;  // Controlled_Buffer controlled_buffer_16
  assign DATA = decoder_1_out12 ? negator_1_out : 8'bz;  // Controlled_Buffer controlled_buffer_17
  assign DATA = decoder_1_out13 ? bit_extender_3_out : 8'bz;  // Controlled_Buffer controlled_buffer_18
  assign DATA = decoder_1_out14 ? bit_extender_4_out : 8'bz;  // Controlled_Buffer controlled_buffer_19
  assign DATA = decoder_1_out15 ? ACC_q : 8'bz;  // Controlled_Buffer controlled_buffer_20
endmodule

module stack (
  input  [7:0] DATA_IN,
  input  CLK,
  input  RESET,
  input  PUSH,
  input  POP,
  input  WRITE_TOS,
  input  READ_TOS,
  output [7:0] DATA_OUT
);

  wire or_1_out;
  wire [7:0] counter_1_q;

  or or_1 (or_1_out, PUSH, POP);
  Counter counter_1 (.clr(RESET), .up(PUSH), .count(or_1_out), .clk(CLK), .Q(counter_1_q));  // open: load, D, carry
  RAM #(.clearpin("true"), .readbehav("war")) ram_1 (
    .addr(counter_1_q), .we(WRITE_TOS), .oe(READ_TOS), .clk(CLK), .din(DATA_IN), .dout(DATA_OUT), .clr(RESET));
endmodule

module mem_reg (
  input  [5:0] ADDR_IN,
  input  [7:0] DATA_IN,
  input  CLK,
  input  RESET,
  input  WRITE_ADDR,
  input  WRITE_MEM,
  input  READ_MEM,
  output [7:0] DATA_OUT
);

  wire [5:0] register_1_q;

  Register #(.width(6)) register_1 (.D(ADDR_IN), .en(WRITE_ADDR), .clk(CLK), .Q(register_1_q), .clr(RESET));
  RAM #(.addrWidth(6), .clearpin("true"), .readbehav("war")) ram_1 (
    .addr(register_1_q), .we(WRITE_MEM), .oe(READ_MEM), .clk(CLK), .din(DATA_IN), .dout(DATA_OUT), .clr(RESET));
endmodule

module t3lc_mem_reg (
  input  CLK,
  input  RESET,
  input  [7:0] ROM_VALUE,
  input  [7:0] DATA_IN,
  output HALTED,
  output [15:0] ROM_ADDR,
  output RAM_WRITE,
  output RAM_READ,
  output [7:0] DATA_OUT,
  output [15:0] RAM_ADDR
);

  wire ALU_AB_READ, ALU_READ, ALU_SD_READ, and_12_out, BRANCH, comparator_1_eq, decoder_2_out9, HALT,
       HALT_qn, IMM_PUSH, JUMP, LAST_IMM_q, not_1_out, not_2_out, OP_IMM_READ, or_1_out, or_2_out, or_3_out,
       or_7_out, POP, PUSH, REG_IMM_READ, REGF_A_ADDR_WRITE, REGF_A_MEM_WRITE, REGF_A_READ,
       REGF_B_ADDR_WRITE, REGF_B_MEM_WRITE, REGF_B_READ, REGF_I_ADDR_WRITE, REGF_I_MEM_WRITE, REGF_I_READ,
       REGF_J_ADDR_WRITE, REGF_J_MEM_WRITE, REGF_J_READ, RESET_ALU, SPECIAL_OP, STACK_READ, STACK_WRITE;
  wire [6:0] REG_IMM;
  wire [7:0] ALU_8_data, bit_extender_1_out, bit_extender_2_out, bit_extender_4_out, controlled_buffer_1_out,
       controlled_buffer_3_out, decoder_1_out0, multiplexer_1_out, multiplexer_2_out, multiplexer_3_out,
       OP_IMM, REGF_A, TOS;
  wire [8:0] bit_extender_3_out, decoder_2_out0;
  wire [15:8] REGF_AB;

  not not_1 (not_1_out, ROM_VALUE[7]);
  assign controlled_buffer_1_out = RAM_READ ? DATA_IN : 8'bz;  // Controlled_Buffer controlled_buffer_1
  Decoder #(.select(3)) decoder_1 (
    .out0(decoder_1_out0[0]), .out1(decoder_1_out0[1]), .out2(decoder_1_out0[2]), .out3(decoder_1_out0[3]),
    .out4(decoder_1_out0[4]), .out5(decoder_1_out0[5]), .out6(decoder_1_out0[6]), .out7(decoder_1_out0[7]),
    .sel(ROM_VALUE[6:4]), .en(not_1_out));
  not not_2 (not_2_out, RAM_READ);
  assign controlled_buffer_1_out = not_2_out ? controlled_buffer_3_out : 8'bz;  // Controlled_Buffer controlled_buffer_2
  assign {RAM_WRITE, REGF_B_ADDR_WRITE, REGF_A_ADDR_WRITE, STACK_WRITE, REGF_J_MEM_WRITE, REGF_I_MEM_WRITE, REGF_B_MEM_WRITE, REGF_A_MEM_WRITE} = decoder_1_out0 & ~bit_extender_1_out;  // AND_Gate and_1, 8 bits wide
  assign bit_extender_1_out = {{7{SPECIAL_OP}}, SPECIAL_OP};  // Bit_Extender bit_extender_1
  Register #(.width(7)) u_REG_IMM (.D(ROM_VALUE[6:0]), .en(ROM_VALUE[7]), .clk(CLK), .Q(REG_IMM), .clr(RESET));
  assign bit_extender_2_out = {{1{1'b0}}, REG_IMM};  // Bit_Extender bit_extender_2
  Multiplexer #(.width(8)) multiplexer_1 (.in0(REGF_A), .in1(TOS), .out(multiplexer_1_out), .sel(ALU_SD_READ));
  Multiplexer #(.width(8)) multiplexer_2 (
    .in0(controlled_buffer_1_out), .in1(bit_extender_2_out), .out(multiplexer_2_out), .sel(IMM_PUSH));
  or or_1 (or_1_out, PUSH, IMM_PUSH);
  or or_2 (or_2_out, IMM_PUSH, STACK_WRITE);
  Multiplexer #(.width(8)) multiplexer_3 (
    .in0(REGF_AB), .in1(controlled_buffer_1_out), .out(multiplexer_3_out), .sel(ALU_SD_READ));
  D_Flip_Flop LAST_IMM (.D(ROM_VALUE[7]), .clk(CLK), .Q(LAST_IMM_q), .reset(RESET));  // open: Qn, preset
  mem_reg u_REGF_A (
    .ADDR_IN(controlled_buffer_1_out[5:0]), .DATA_IN(controlled_buffer_1_out), .CLK(CLK), .RESET(RESET),
    .WRITE_ADDR(REGF_A_ADDR_WRITE), .WRITE_MEM(REGF_A_MEM_WRITE), .READ_MEM(REGF_A_READ), .DATA_OUT(REGF_A));
  mem_reg REGF_B (
    .ADDR_IN(controlled_buffer_1_out[5:0]), .DATA_IN(controlled_buffer_1_out), .CLK(CLK), .RESET(RESET),
    .WRITE_ADDR(REGF_B_ADDR_WRITE), .WRITE_MEM(REGF_B_MEM_WRITE), .READ_MEM(REGF_B_READ), .DATA_OUT(REGF_AB));
  mem_reg REGF_I (
    .ADDR_IN(REG_IMM[5:0]), .DATA_IN(controlled_buffer_1_out), .CLK(CLK), .RESET(RESET),
    .WRITE_ADDR(REGF_A_ADDR_WRITE), .WRITE_MEM(REGF_A_MEM_WRITE), .READ_MEM(REGF_A_READ),
    .DATA_OUT(RAM_ADDR[7:0]));
  mem_reg REGF_J (
    .ADDR_IN(REG_IMM[5:0]), .DATA_IN(controlled_buffer_1_out), .CLK(CLK), .RESET(RESET),
    .WRITE_ADDR(REGF_B_ADDR_WRITE), .WRITE_MEM(REGF_B_MEM_WRITE), .READ_MEM(REGF_B_READ),
    .DATA_OUT(RAM_ADDR[15:8]));
  or or_3 (or_3_out, RESET_ALU, RESET);
  and and_2 (IMM_PUSH, ROM_VALUE[7], LAST_IMM_q);
  Decoder #(.select(4)) decoder_2 (
    .out0(decoder_2_out0[0]), .out1(decoder_2_out0[1]), .out2(decoder_2_out0[2]), .out3(decoder_2_out0[3]),
    .out4(decoder_2_out0[4]), .out5(decoder_2_out0[5]), .out6(decoder_2_out0[6]), .out7(decoder_2_out0[7]),
    .out8(decoder_2_out0[8]), .out9(decoder_2_out9), .out10(OP_IMM[7]), .out11(OP_IMM[6]), .out12(OP_IMM[5]),
    .out13(OP_IMM[4]), .out14(OP_IMM[3]), .out15(OP_IMM[0]), .sel(ROM_VALUE[3:0]), .en(not_1_out));
  assign bit_extender_3_out = {{8{SPECIAL_OP}}, SPECIAL_OP};  // Bit_Extender bit_extender_3
  stack STACK_MEM (
    .CLK(CLK), .RESET(RESET), .PUSH(or_1_out), .POP(POP), .DATA_IN(multiplexer_2_out), .WRITE_TOS(or_2_out),
    .READ_TOS(STACK_READ), .DATA_OUT(TOS));
  alu ALU_8 (
    .ENA(ALU_READ), .OP(REG_IMM[4:0]), .CLK(CLK), .RESET(or_3_out), .A(multiplexer_1_out),
    .B(multiplexer_3_out), .DATA(ALU_8_data));
  and and_3 (HALT, decoder_2_out0[0], decoder_1_out0[0]);
  and and_4 (PUSH, decoder_2_out0[1], decoder_1_out0[1]);
  and and_5 (POP, decoder_2_out0[2], decoder_1_out0[2]);
  and and_6 (RESET_ALU, decoder_2_out0[3], decoder_1_out0[3]);
  and and_7 (BRANCH, decoder_2_out0[4], decoder_1_out0[4]);
  and and_8 (JUMP, decoder_2_out0[5], decoder_1_out0[5]);
  and and_9 (REGF_I_ADDR_WRITE, decoder_2_out0[6], decoder_1_out0[6]);
  and and_10 (REGF_J_ADDR_WRITE, decoder_2_out0[7], decoder_1_out0[7]);
  assign {REG_IMM_READ, RAM_READ, ALU_SD_READ, ALU_AB_READ, STACK_READ, REGF_J_READ, REGF_I_READ, REGF_B_READ, REGF_A_READ} = decoder_2_out0 & ~bit_extender_3_out;  // AND_Gate and_11, 9 bits wide
  assign bit_extender_4_out = {{1{1'b0}}, REG_IMM};  // Bit_Extender bit_extender_4
  or or_4 (OP_IMM_READ, decoder_2_out9, OP_IMM[7], OP_IMM[6], OP_IMM[5], OP_IMM[4], OP_IMM[3], OP_IMM[0]);
  or or_5 (SPECIAL_OP, HALT, PUSH, POP, RESET_ALU, BRANCH, JUMP, REGF_I_ADDR_WRITE, REGF_J_ADDR_WRITE);
  or or_6 (ALU_READ, ALU_AB_READ, ALU_SD_READ);
  assign controlled_buffer_3_out = OP_IMM_READ ? {OP_IMM[7:3], 2'b00, OP_IMM[0]} : 8'bz;  // Controlled_Buffer controlled_buffer_3
  assign controlled_buffer_3_out = REG_IMM_READ ? bit_extender_4_out : 8'bz;  // Controlled_Buffer controlled_buffer_4
  assign DATA_OUT = RAM_WRITE ? controlled_buffer_3_out : 8'bz;  // Controlled_Buffer controlled_buffer_5
  assign controlled_buffer_3_out = REGF_A_READ ? REGF_A : 8'bz;  // Controlled_Buffer controlled_buffer_6
  assign controlled_buffer_3_out = REGF_B_READ ? REGF_AB : 8'bz;  // Controlled_Buffer controlled_buffer_7
  assign controlled_buffer_3_out = REGF_I_READ ? RAM_ADDR[7:0] : 8'bz;  // Controlled_Buffer controlled_buffer_8
  assign controlled_buffer_3_out = REGF_J_READ ? RAM_ADDR[15:8] : 8'bz;  // Controlled_Buffer controlled_buffer_9
  assign controlled_buffer_3_out = STACK_READ ? TOS : 8'bz;  // Controlled_Buffer controlled_buffer_10
  assign controlled_buffer_3_out = ALU_READ ? ALU_8_data : 8'bz;  // Controlled_Buffer controlled_buffer_11
  Comparator comparator_1 (.a(TOS), .b({8{1'b0}}), .eq(comparator_1_eq));  // open: gt, lt
  D_Flip_Flop u_HALT (.D(HALT), .clk(CLK), .Q(HALTED), .Qn(HALT_qn), .reset(RESET));  // open: preset
  and and_12 (and_12_out, BRANCH, comparator_1_eq);
  or or_7 (or_7_out, JUMP, and_12_out);
  Counter #(.max('hffff), .width(16)) CNT_PC (
    .load(or_7_out), .D(RAM_ADDR), .count(HALT_qn), .Q(ROM_ADDR), .clk(CLK), .clr(RESET));  // open: carry, up

  // Other names for the same wires on the sheet: REGF_AB[7:0] = REGF_A; REGF_B[7:0] = REGF_AB;
  //   REGF_I[7:0] = RAM_ADDR[7:0]; REGF_IJ[15:0] = RAM_ADDR; REGF_J[7:0] = RAM_ADDR[15:8]

  // Notes on the sheet:
  //   DATA BUS TARGET
  //   DATA BUS SOURCE
endmodule

module test_t3lc_mem_reg (
  input  RESET
);

  wire CLK_out, t3lc_mem_reg_1_halted, t3lc_mem_reg_1_ram_read, t3lc_mem_reg_1_ram_write;
  wire [7:0] controlled_buffer_1_out, ram_1_dout, rom_1_data, t3lc_mem_reg_1_data_out;
  wire [15:0] t3lc_mem_reg_1_ram_addr, t3lc_mem_reg_1_rom_addr;

  Clock CLK (.out(CLK_out));
  ROM #(.addrWidth(16)) rom_1 (.addr(t3lc_mem_reg_1_rom_addr), .data(rom_1_data));
  t3lc_mem_reg t3lc_mem_reg_1 (
    .CLK(CLK_out), .RESET(RESET), .ROM_VALUE(rom_1_data), .DATA_IN(controlled_buffer_1_out),
    .RAM_READ(t3lc_mem_reg_1_ram_read), .DATA_OUT(t3lc_mem_reg_1_data_out), .HALTED(t3lc_mem_reg_1_halted),
    .ROM_ADDR(t3lc_mem_reg_1_rom_addr), .RAM_WRITE(t3lc_mem_reg_1_ram_write),
    .RAM_ADDR(t3lc_mem_reg_1_ram_addr));
  LED led_1 (.in(t3lc_mem_reg_1_halted));
  RAM #(.addrWidth(16)) ram_1 (
    .addr(t3lc_mem_reg_1_ram_addr), .we(t3lc_mem_reg_1_ram_write), .oe(t3lc_mem_reg_1_ram_read),
    .clk(CLK_out), .din(t3lc_mem_reg_1_data_out), .dout(ram_1_dout));
  assign controlled_buffer_1_out = t3lc_mem_reg_1_ram_read ? ram_1_dout : 8'bz;  // Controlled_Buffer controlled_buffer_1
endmodule

module t3lc_regs (
  input  CLK,
  input  RESET,
  input  [7:0] ROM_VALUE,
  input  [7:0] DATA_IN,
  output HALTED,
  output [15:0] ROM_ADDR,
  output [7:0] DATA_OUT,
  output [15:0] ADDR,
  output NOP0,
  output NOP1,
  output PERI0_WRITE,
  output PERI0_READ,
  output PERI1_WRITE,
  output PERI1_READ,
  output RAM_WRITE,
  output RAM_READ,
  output [7:0] REG_I_OUT,
  output [7:0] REG_J_OUT
);

  wire ALU_READ, BRANCH, BRANCH_JUMP, comparator_1_eq, decoder_2_out10, HALT, HALT_qn, IMM_PUSH, JUMP,
       LAST_IMM_q, not_1_out, not_2_out, or_2_out, or_3_out, or_4_out, or_7_out, or_8_out, or_9_out, POP,
       PUSH, READ_EXT, REG_A_READ, REG_A_WRITE, REG_B_READ, REG_B_WRITE, REG_I_READ, REG_I_WRITE,
       REG_IMM_READ, REG_J_READ, REG_J_WRITE, RESET_ALU, SPECIAL_OP, STACK_READ, STACK_WRITE, WRITE_EXT;
  wire [6:0] REG_IMM;
  wire [7:0] alu_1_data, bit_extender_1_out, bit_extender_2_out, bit_extender_4_out, controlled_buffer_1_out,
       controlled_buffer_2_out, controlled_buffer_3_out, decoder_1_out0, decoder_2_out11, multiplexer_1_out,
       REG_A_q, REG_B_q, TOS;
  wire [9:0] bit_extender_3_out, decoder_2_out0;
  wire [15:0] REGF_AB;

  not not_1 (not_1_out, ROM_VALUE[7]);
  Decoder #(.select(3)) decoder_1 (
    .out0(decoder_1_out0[0]), .out1(decoder_1_out0[1]), .out2(decoder_1_out0[2]), .out3(decoder_1_out0[3]),
    .out4(decoder_1_out0[4]), .out5(decoder_1_out0[5]), .out6(decoder_1_out0[6]), .out7(decoder_1_out0[7]),
    .sel(ROM_VALUE[6:4]), .en(not_1_out));
  not not_2 (not_2_out, READ_EXT);
  assign controlled_buffer_1_out = not_2_out ? controlled_buffer_3_out : 8'bz;  // Controlled_Buffer controlled_buffer_1
  assign controlled_buffer_2_out = READ_EXT ? DATA_IN : 8'bz;  // Controlled_Buffer controlled_buffer_2
  assign {RAM_WRITE, PERI1_WRITE, PERI0_WRITE, REG_J_WRITE, REG_I_WRITE, STACK_WRITE, REG_B_WRITE, REG_A_WRITE} = decoder_1_out0 & ~bit_extender_1_out;  // AND_Gate and_1, 8 bits wide
  assign bit_extender_1_out = {{7{SPECIAL_OP}}, SPECIAL_OP};  // Bit_Extender bit_extender_1
  Register #(.width(7)) u_REG_IMM (.D(ROM_VALUE[6:0]), .en(ROM_VALUE[7]), .clk(CLK), .Q(REG_IMM), .clr(RESET));
  Register REG_A (.D(controlled_buffer_2_out), .en(REG_A_WRITE), .clk(CLK), .Q(REG_A_q), .clr(RESET));
  Register REG_B (.D(controlled_buffer_1_out), .en(REG_B_WRITE), .clk(CLK), .Q(REG_B_q), .clr(RESET));
  Register REG_I (.D(controlled_buffer_1_out), .en(REG_I_WRITE), .clk(CLK), .Q(REG_I_OUT), .clr(RESET));
  Register REG_J (.D(controlled_buffer_1_out), .en(REG_J_WRITE), .clk(CLK), .Q(REG_J_OUT), .clr(RESET));
  assign bit_extender_2_out = {{1{1'b0}}, REG_IMM};  // Bit_Extender bit_extender_2
  D_Flip_Flop LAST_IMM (.D(ROM_VALUE[7]), .clk(CLK), .Q(LAST_IMM_q), .reset(RESET));  // open: Qn, preset
  or or_1 (WRITE_EXT, PERI0_WRITE, PERI1_WRITE, RAM_WRITE);
  Multiplexer #(.width(8)) multiplexer_1 (
    .in0(controlled_buffer_1_out), .in1(bit_extender_2_out), .out(multiplexer_1_out), .sel(IMM_PUSH));
  or or_2 (or_2_out, PUSH, IMM_PUSH);
  or or_3 (or_3_out, IMM_PUSH, STACK_WRITE);
  and and_2 (IMM_PUSH, ROM_VALUE[7], LAST_IMM_q);
  Decoder #(.select(4)) decoder_2 (
    .out0(decoder_2_out0[0]), .out1(decoder_2_out0[1]), .out2(decoder_2_out0[2]), .out3(decoder_2_out0[3]),
    .out4(decoder_2_out0[4]), .out5(decoder_2_out0[5]), .out6(decoder_2_out0[6]), .out7(decoder_2_out0[7]),
    .out8(decoder_2_out0[8]), .out9(decoder_2_out0[9]), .out10(decoder_2_out10), .out11(decoder_2_out11[0]),
    .out12(decoder_2_out11[1]), .out13(decoder_2_out11[2]), .out14(decoder_2_out11[3]),
    .out15(decoder_2_out11[7]), .sel(ROM_VALUE[3:0]), .en(not_1_out));
  assign bit_extender_3_out = {{9{SPECIAL_OP}}, SPECIAL_OP};  // Bit_Extender bit_extender_3
  or or_4 (or_4_out, RESET_ALU, RESET);
  and and_3 (HALT, decoder_2_out0[0], decoder_1_out0[0]);
  and and_4 (PUSH, decoder_2_out0[1], decoder_1_out0[1]);
  and and_5 (POP, decoder_2_out0[2], decoder_1_out0[2]);
  and and_6 (RESET_ALU, decoder_2_out0[3], decoder_1_out0[3]);
  and and_7 (BRANCH, decoder_2_out0[4], decoder_1_out0[4]);
  and and_8 (JUMP, decoder_2_out0[5], decoder_1_out0[5]);
  and and_9 (NOP0, decoder_2_out0[6], decoder_1_out0[6]);
  and and_10 (NOP1, decoder_2_out0[7], decoder_1_out0[7]);
  assign {REG_IMM_READ, ALU_READ, RAM_READ, PERI1_READ, PERI0_READ, REG_J_READ, REG_I_READ, STACK_READ, REG_B_READ, REG_A_READ} = decoder_2_out0 & ~bit_extender_3_out;  // AND_Gate and_11, 10 bits wide
  stack STACK_MEM (
    .CLK(CLK), .RESET(RESET), .PUSH(or_2_out), .POP(POP), .DATA_IN(multiplexer_1_out), .WRITE_TOS(or_3_out),
    .READ_TOS(STACK_READ), .DATA_OUT(TOS));
  or or_5 (SPECIAL_OP, HALT, PUSH, POP, RESET_ALU, BRANCH, JUMP, NOP0, NOP1);
  assign bit_extender_4_out = {{1{1'b0}}, REG_IMM};  // Bit_Extender bit_extender_4
  assign controlled_buffer_3_out = REG_IMM_READ ? bit_extender_4_out : 8'bz;  // Controlled_Buffer controlled_buffer_3
  or or_6 (READ_EXT, PERI0_READ, PERI1_READ, RAM_READ);
  assign controlled_buffer_3_out = REG_A_READ ? REG_A_q : 8'bz;  // Controlled_Buffer controlled_buffer_4
  assign controlled_buffer_3_out = ALU_READ ? alu_1_data : 8'bz;  // Controlled_Buffer controlled_buffer_5
  alu alu_1 (
    .ENA(ALU_READ), .OP(REG_IMM[4:0]), .CLK(CLK), .RESET(or_4_out), .A(REG_A_q), .B(REG_B_q),
    .DATA(alu_1_data));
  assign controlled_buffer_3_out = REG_B_READ ? REG_B_q : 8'bz;  // Controlled_Buffer controlled_buffer_6
  assign controlled_buffer_3_out = STACK_READ ? TOS : 8'bz;  // Controlled_Buffer controlled_buffer_7
  assign controlled_buffer_3_out = STACK_READ ? REG_I_OUT : 8'bz;  // Controlled_Buffer controlled_buffer_8
  assign controlled_buffer_3_out = STACK_READ ? REG_J_OUT : 8'bz;  // Controlled_Buffer controlled_buffer_9
  or or_7 (or_7_out, decoder_2_out11[7], decoder_2_out11[3], decoder_2_out11[2], decoder_2_out11[1], decoder_2_out11[0], decoder_2_out10);
  assign controlled_buffer_3_out = or_7_out ? {decoder_2_out11[7], 3'b000, decoder_2_out11[3:0]} : 8'bz;  // Controlled_Buffer controlled_buffer_10
  assign DATA_OUT = WRITE_EXT ? controlled_buffer_3_out : 8'bz;  // Controlled_Buffer controlled_buffer_11
  D_Flip_Flop u_HALT (.D(HALT), .clk(CLK), .Q(HALTED), .Qn(HALT_qn), .reset(RESET));  // open: preset
  or or_8 (or_8_out, READ_EXT, WRITE_EXT);
  assign ADDR = or_8_out ? REGF_AB : 16'bz;  // Controlled_Buffer controlled_buffer_12
  Comparator comparator_1 (.a(TOS), .b({8{1'b0}}), .eq(comparator_1_eq));  // open: gt, lt
  or or_9 (or_9_out, JUMP, BRANCH_JUMP);
  Counter #(.max('hffff), .width(16)) CNT_PC (
    .load(or_9_out), .D(REGF_AB), .count(HALT_qn), .Q(ROM_ADDR), .clk(CLK), .clr(RESET));  // open: carry, up
  and and_12 (BRANCH_JUMP, BRANCH, comparator_1_eq);

  // Notes on the sheet:
  //   DATA BUS TARGET
  //   DATA BUS SOURCE
endmodule
